// Logisim project 8bitCPU.circ as structural Verilog: 15 circuits, main circuit main
module main (
  input  ENABLE,
  input  MANUAL_TICK,
  input  in_3,
  input  in_4,
  output [4:0] out_5,
  output [4:0] out_6,
  output [4:0] out_7,
  output [7:0] out_8,
  output [7:0] out_9,
  output [7:0] out_10,
  output [7:0] out_11,
  output [7:0] out_12,
  output [7:0] out_13,
  output [7:0] out_14
);

  wire A_IN, ACC_IN, ACC_OUT, ALU_OUT, B_IN, B_REG_OUT, clk_1_clk_out, clock_1_out, COUNTER_ENB, COUNTER_OUT,
       decoder_1_out0, decoder_1_out1, decoder_1_out2, decoder_1_out3, decoder_1_out4, decoder_1_out5,
       decoder_1_out6, decoder_1_out7, decoder_1_out8, decoder_1_out9, HALT, INR_IN, INR_OUT, MAR_IN,
       MBR_IN_IN, MBR_IN_OUT, MBR_OUT_IN, MBR_OUT_OUT, not_1_out, ONE, or_1_out, or_2_out,
       pull_resistor_1_node, pull_resistor_2_node, RAM_OUT, RESET_out, STORE_RAM, SUB;
  wire [3:0] step_counter_1_binary_out;
  wire [7:0] alu_1_alu_data_out, mbr_in_1_out_7, memory_1_always_out, memory_1_ram_out,
       program_counter_1_address_out;
  wire [7:7] pull_resistor_3_node;

  not not_1 (not_1_out, clk_1_clk_out);
  or or_1 (or_1_out, RESET_out, decoder_1_out9);
  STEP_COUNTER step_counter_1 (.RESET(or_1_out), .BINARY_OUT(step_counter_1_binary_out), .CLOCK(not_1_out));
  or or_2 (or_2_out, RESET_out, decoder_1_out9);
  LED led_1 (.in(decoder_1_out0));
  Decoder #(.select(4), .enable("false")) decoder_1 (
    .out0(decoder_1_out0), .out1(decoder_1_out1), .out2(decoder_1_out2), .out3(decoder_1_out3),
    .out4(decoder_1_out4), .out5(decoder_1_out5), .out6(decoder_1_out6), .out7(decoder_1_out7),
    .out8(decoder_1_out8), .out9(decoder_1_out9), .sel(step_counter_1_binary_out));  // open: out10, out11, out12, out13, out14, out15
  LED led_2 (.in(decoder_1_out4));
  LED led_3 (.in(decoder_1_out2));
  LED led_4 (.in(decoder_1_out1));
  LED led_5 (.in(decoder_1_out3));
  Clock clock_1 (.out(clock_1_out));
  PROGRAM_COUNTER program_counter_1 (
    .RESET(RESET_out), .JUMP(in_4), .ALWAYS_OUT(out_6), .COUNTER_ENABLE(COUNTER_ENB), .CLOCK(clk_1_clk_out),
    .ADDRESS_IN(program_counter_1_address_out[4:0]), .COUNTER_OUT(COUNTER_OUT),
    .ADDRESS_OUT(program_counter_1_address_out[4:0]));
  LED led_6 (.in(decoder_1_out5));
  LED led_7 (.in(decoder_1_out8));
  LED led_8 (.in(decoder_1_out6));
  LED led_9 (.in(decoder_1_out7));
  CLK clk_1 (.CLK_IN(clock_1_out), .CLK_ENB(ENABLE), .MANUAL_CLK(MANUAL_TICK), .CLK_OUT(clk_1_clk_out), .in_4(HALT));
  INSTRUCTION_REGISTER instruction_register_1 (
    .ALWAYS_OUT(out_8), .DATA_IN(program_counter_1_address_out), .STORE(INR_IN), .DATA_OUT_ENABLE(INR_OUT),
    .RESET(or_2_out), .CLOCK(clk_1_clk_out), .DATA_OUT(program_counter_1_address_out));
  Hex_Digit_Display hex_digit_display_1 (.value(out_11[7:4]), .dp(pull_resistor_1_node));
  Pull_Resistor pull_resistor_1 (.node(pull_resistor_1_node));
  ACC_REGISTER acc_register_1 (
    .ALWAYS_OUT(out_11), .DATA_IN(program_counter_1_address_out), .DATA_OUT(program_counter_1_address_out),
    .ACC_IN(ACC_IN), .ACC_OUT(ACC_OUT), .CLOCK(clk_1_clk_out), .ACC_RESET(RESET_out));
  ROM #(.dataWidth(10)) rom_1 (
    .addr({pull_resistor_3_node[7], out_8[7:5], step_counter_1_binary_out}),
    .data({B_IN, SUB, STORE_RAM, A_IN, ALU_OUT, COUNTER_ENB, COUNTER_OUT, B_REG_OUT, ACC_OUT, ACC_IN}));  // open: sel
  ROM #(.dataWidth(10)) rom_2 (
    .addr({pull_resistor_3_node[7], out_8[7:5], step_counter_1_binary_out}),
    .data({MAR_IN, HALT, RAM_OUT, INR_OUT, INR_IN, ONE, MBR_IN_OUT, MBR_OUT_OUT, MBR_IN_IN, MBR_OUT_IN}));  // open: sel
  Button RESET (.out(RESET_out));
  Hex_Digit_Display hex_digit_display_2 (.value(out_11[3:0]), .dp(pull_resistor_2_node));
  Pull_Resistor pull_resistor_2 (.node(pull_resistor_2_node));
  Pull_Resistor pull_resistor_3 (.node(pull_resistor_3_node[7]));
  LED led_10 (.in(program_counter_1_address_out[7]));
  LED led_11 (.in(program_counter_1_address_out[6]));
  LED led_12 (.in(program_counter_1_address_out[5]));
  Pull_Resistor pull_resistor_4 (.node(program_counter_1_address_out[7]));
  Pull_Resistor pull_resistor_5 (.node(program_counter_1_address_out[6]));
  Pull_Resistor pull_resistor_6 (.node(program_counter_1_address_out[5]));
  LED led_13 (.in(program_counter_1_address_out[3]));
  LED led_14 (.in(program_counter_1_address_out[1]));
  LED led_15 (.in(program_counter_1_address_out[4]));
  LED led_16 (.in(program_counter_1_address_out[2]));
  Pull_Resistor pull_resistor_7 (.node(program_counter_1_address_out[4]));
  Pull_Resistor pull_resistor_8 (.node(program_counter_1_address_out[1]));
  Pull_Resistor pull_resistor_9 (.node(program_counter_1_address_out[3]));
  Pull_Resistor pull_resistor_10 (.node(program_counter_1_address_out[2]));
  LED led_17 (.in(program_counter_1_address_out[0]));
  REGISTER_B register_b_1 (
    .DATA_IN(alu_1_alu_data_out), .DATA_OUT(program_counter_1_address_out), .STORE(B_IN),
    .CLOCK(clk_1_clk_out), .RESET(RESET_out), .in_3(B_REG_OUT), .ALWAYS_OUT(out_13));
  Pull_Resistor pull_resistor_11 (.node(program_counter_1_address_out[0]));
  LED led_18 (.in(B_IN));
  LED led_19 (.in(SUB));
  LED led_20 (.in(STORE_RAM));
  LED led_21 (.in(A_IN));
  LED led_22 (.in(B_REG_OUT));
  LED led_23 (.in(COUNTER_OUT));
  LED led_24 (.in(ALU_OUT));
  LED led_25 (.in(COUNTER_ENB));
  MAR mar_1 (
    .ALWAYS_OUT(out_5), .DATA_IN(program_counter_1_address_out[4:0]), .MAR_IN(MAR_IN), .MAR_OUT(in_3),
    .CLOCK(clk_1_clk_out), .MAR_RESET(RESET_out), .DATA_OUT(program_counter_1_address_out[4:0]));
  A_Register a_register_1 (
    .ALWAYS_OUT(out_10), .DATA_IN(program_counter_1_address_out), .A_IN(A_IN), .CLOCK(clk_1_clk_out),
    .A_RESET(RESET_out));
  ALU alu_1 (
    .A_IN(out_10), .ALWAYS_OUT(out_12), .B_IN(program_counter_1_address_out),
    .ALU_DATA_OUT(alu_1_alu_data_out), .OUTPUT_ENB(ALU_OUT), .SUB(SUB), .in_4(ONE));  // open: COUT, out_11, out_10, in_1
  LED led_26 (.in(ACC_IN));
  LED led_27 (.in(ACC_OUT));
  LED led_28 (.in(memory_1_always_out[7]));
  MBR mbr_1 (
    .DATA_IN(memory_1_ram_out), .MBR_IN(MBR_OUT_IN), .CLOCK(clk_1_clk_out), .MBR_RESET(RESET_out),
    .ALWAYS_OUT(out_9), .out_7(program_counter_1_address_out), .MBR_OUT(MBR_OUT_OUT));
  MBR_IN mbr_in_1 (
    .DATA_IN(program_counter_1_address_out), .MBR_IN(MBR_IN_IN), .CLOCK(clk_1_clk_out),
    .MBR_RESET(RESET_out), .ALWAYS_OUT(out_14), .out_7(mbr_in_1_out_7), .MBR_OUT(MBR_IN_OUT));
  LED led_29 (.in(out_5[4]));
  LED led_30 (.in(memory_1_always_out[6]));
  LED led_31 (.in(memory_1_always_out[3]));
  LED led_32 (.in(memory_1_always_out[5]));
  LED led_33 (.in(memory_1_always_out[4]));
  LED led_34 (.in(MAR_IN));
  LED led_35 (.in(out_5[1]));
  LED led_36 (.in(out_5[0]));
  LED led_37 (.in(out_5[2]));
  LED led_38 (.in(out_5[3]));
  LED led_39 (.in(memory_1_always_out[0]));
  LED led_40 (.in(memory_1_always_out[2]));
  LED led_41 (.in(memory_1_always_out[1]));
  LED led_42 (.in(INR_OUT));
  LED led_43 (.in(RAM_OUT));
  LED led_44 (.in(HALT));
  MEMORY memory_1 (
    .ADDRESS(out_5), .DATA(mbr_in_1_out_7), .STORE(STORE_RAM), .ALWAYS_OUT(memory_1_always_out),
    .RAM_OUT_ENB(RAM_OUT), .CLK(clk_1_clk_out), .RAM_OUT(memory_1_ram_out));
  LED led_45 (.in(ONE));
  LED led_46 (.in(MBR_IN_OUT));
  LED led_47 (.in(INR_IN));
  LED led_48 (.in(MBR_IN_IN));
  LED led_49 (.in(MBR_OUT_IN));
  LED led_50 (.in(MBR_OUT_OUT));

  assign out_7 = out_5;

  // Notes on the sheet:
  //   T0
  //   T2
  //   T1
  //   T4
  //   T3
  //   T7
  //   T6
  //   T5
  //   T8
  //   contents of rom_1 (hex, n*v repeats v):
  //   8 0 10 0 0 1 10*0 8 0 0 0 2 80 13*0 322 5 5 222 5 11*0 42 220 5 12*0 10 0 0 40 222 5 153*0 80
  //   contents of rom_2 (hex, n*v repeats v):
  //   200 81 24 240 81 4 10*0 200 81 240 240 2 8 30*0 10 13*0 24 240 81 4 45*0 100
endmodule

module CLK (
  input  CLK_IN,
  input  CLK_ENB,
  input  MANUAL_CLK,
  input  in_4,
  output CLK_OUT
);

  wire and_1_out, and_2_out, not_1_out, not_2_out, or_1_out;

  not not_1 (not_1_out, CLK_ENB);
  and and_1 (and_1_out, CLK_IN, CLK_ENB);
  and and_2 (and_2_out, not_1_out, MANUAL_CLK);
  not not_2 (not_2_out, in_4);
  or or_1 (or_1_out, and_1_out, and_2_out);
  assign CLK_OUT = not_2_out ? or_1_out : 1'bz;  // Controlled_Buffer controlled_buffer_1
endmodule

module PROGRAM_COUNTER (
  input  JUMP,
  input  [4:0] ADDRESS_IN,
  input  COUNTER_ENABLE,
  input  CLOCK,
  input  RESET,
  input  COUNTER_OUT,
  output [4:0] ALWAYS_OUT,
  output [4:0] ADDRESS_OUT
);

  Counter #(.width(5), .max('h1f)) counter_1 (
    .load(JUMP), .D(ADDRESS_IN), .count(COUNTER_ENABLE), .Q(ALWAYS_OUT), .clk(CLOCK), .clr(RESET));  // open: carry
  assign ADDRESS_OUT = COUNTER_OUT ? ALWAYS_OUT : 5'bz;  // Controlled_Buffer controlled_buffer_1
endmodule

module A_Register (
  input  [7:0] DATA_IN,
  input  A_IN,
  input  CLOCK,
  input  A_RESET,
  output [7:0] ALWAYS_OUT
);

  Register register_1 (.D(DATA_IN), .en(A_IN), .Q(ALWAYS_OUT), .clk(CLOCK), .clr(A_RESET));
endmodule

module ALU (
  input  in_1,
  input  [7:0] A_IN,
  input  [7:0] B_IN,
  input  in_4,
  input  OUTPUT_ENB,
  input  SUB,
  output [7:0] ALWAYS_OUT,
  output [7:0] ALU_DATA_OUT,
  output COUT,
  output [7:0] out_10,
  output [7:0] out_11
);

  wire not_1_out;
  wire [7:0] controlled_buffer_1_out, multiplexer_1_out;

  assign controlled_buffer_1_out = SUB ? {8{1'b1}} : 8'bz;  // Controlled_Buffer controlled_buffer_1
  Multiplexer #(.width(8), .enable("false")) multiplexer_1 (
    .in0(B_IN), .in1(8'h1), .out(multiplexer_1_out), .sel(in_4));
  assign controlled_buffer_1_out = not_1_out ? {8{1'b0}} : 8'bz;  // Controlled_Buffer controlled_buffer_2
  not not_1 (not_1_out, SUB);
  assign out_11 = multiplexer_1_out ^ controlled_buffer_1_out;  // XOR_Gate xor_1, 8 bits wide
  Adder adder_1 (.a(A_IN), .b(out_11), .out(ALWAYS_OUT), .cin(in_1), .cout(COUT));
  assign ALU_DATA_OUT = OUTPUT_ENB ? ALWAYS_OUT : 8'bz;  // Controlled_Buffer controlled_buffer_3

  assign out_10 = ALWAYS_OUT;
endmodule

module REGISTER_B (
  input  [7:0] DATA_IN,
  input  STORE,
  input  in_3,
  input  CLOCK,
  input  RESET,
  output [7:0] ALWAYS_OUT,
  output [7:0] DATA_OUT
);

  Register register_1 (.D(DATA_IN), .en(STORE), .Q(ALWAYS_OUT), .clk(CLOCK), .clr(RESET));
  assign DATA_OUT = in_3 ? ALWAYS_OUT : 8'bz;  // Controlled_Buffer controlled_buffer_1
endmodule

module ACC_REGISTER (
  input  [7:0] DATA_IN,
  input  ACC_IN,
  input  ACC_OUT,
  input  CLOCK,
  input  ACC_RESET,
  output [7:0] ALWAYS_OUT,
  output [7:0] DATA_OUT
);

  Register register_1 (.D(DATA_IN), .en(ACC_IN), .Q(ALWAYS_OUT), .clk(CLOCK), .clr(ACC_RESET));
  assign DATA_OUT = ACC_OUT ? ALWAYS_OUT : 8'bz;  // Controlled_Buffer controlled_buffer_1
endmodule

module MAR (
  input  [4:0] DATA_IN,
  input  MAR_IN,
  input  MAR_OUT,
  input  CLOCK,
  input  MAR_RESET,
  output [4:0] ALWAYS_OUT,
  output [4:0] DATA_OUT
);

  Register #(.width(5), .trigger("high")) register_1 (
    .D(DATA_IN), .en(MAR_IN), .Q(ALWAYS_OUT), .clk(CLOCK), .clr(MAR_RESET));
  assign DATA_OUT = MAR_OUT ? ALWAYS_OUT : 5'bz;  // Controlled_Buffer controlled_buffer_1
endmodule

module MEMORY (
  input  [4:0] ADDRESS,
  input  [7:0] DATA,
  input  STORE,
  input  RAM_OUT_ENB,
  input  CLK,
  output [7:0] ALWAYS_OUT,
  output [7:0] RAM_OUT
);

  RAM #(.addrWidth(5), .bus("separate")) ram_1 (
    .addr(ADDRESS), .din(DATA), .data(ALWAYS_OUT), .str(STORE), .clk(CLK));  // open: sel, ld, clr
  assign RAM_OUT = RAM_OUT_ENB ? ALWAYS_OUT : 8'bz;  // Controlled_Buffer controlled_buffer_1
endmodule

module INSTRUCTION_REGISTER (
  input  [7:0] DATA_IN,
  input  STORE,
  input  DATA_OUT_ENABLE,
  input  RESET,
  input  CLOCK,
  output [7:0] ALWAYS_OUT,
  output [7:0] DATA_OUT
);

  wire [7:4] pull_resistor_1_node;

  Register register_1 (.D(DATA_IN), .en(STORE), .Q(ALWAYS_OUT), .clk(CLOCK), .clr(RESET));
  Pull_Resistor pull_resistor_1 (.node(pull_resistor_1_node[4]));
  Pull_Resistor pull_resistor_2 (.node(pull_resistor_1_node[5]));
  Pull_Resistor pull_resistor_3 (.node(pull_resistor_1_node[6]));
  Pull_Resistor pull_resistor_4 (.node(pull_resistor_1_node[7]));
  assign DATA_OUT = DATA_OUT_ENABLE ? {pull_resistor_1_node, ALWAYS_OUT[3:0]} : 8'bz;  // Controlled_Buffer controlled_buffer_1
endmodule

module STEP_COUNTER (
  input  RESET,
  input  CLOCK,
  output [3:0] BINARY_OUT
);

  Counter #(.width(4), .max('hf)) counter_1 (
    .count(1'b1), .Q(BINARY_OUT), .clk(CLOCK), .clr(RESET));  // open: load, D, carry
endmodule

module zero_flag (
  input  [7:0] in_1,
  output ZERO
);

  wire and_1_out, and_2_out, nor_1_out, nor_2_out, nor_3_out, nor_4_out;

  nor nor_1 (nor_1_out, in_1[0], in_1[1]);
  nor nor_2 (nor_2_out, in_1[2], in_1[3]);
  nor nor_3 (nor_3_out, in_1[4], in_1[5]);
  nor nor_4 (nor_4_out, in_1[6], in_1[7]);
  and and_1 (and_1_out, nor_1_out, nor_2_out);
  and and_2 (and_2_out, nor_3_out, nor_4_out);
  and and_3 (ZERO, and_1_out, and_2_out);
endmodule

module FLAGS (
  input  CARRY,
  input  ZERO,
  input  STORE,
  input  CLOCK,
  input  RESET,
  output CARRY_OUT,
  output ZERO_OUT
);

  Register #(.width(1)) register_1 (.D(CARRY), .en(STORE), .Q(CARRY_OUT), .clk(CLOCK), .clr(RESET));
  Register #(.width(1)) register_2 (.D(ZERO), .en(STORE), .Q(ZERO_OUT), .clk(CLOCK), .clr(RESET));
endmodule

module MBR (
  input  [7:0] DATA_IN,
  input  MBR_IN,
  input  MBR_OUT,
  input  CLOCK,
  input  MBR_RESET,
  output [7:0] ALWAYS_OUT,
  output [7:0] out_7
);

  Register register_1 (.D(DATA_IN), .en(MBR_IN), .Q(ALWAYS_OUT), .clk(CLOCK), .clr(MBR_RESET));
  assign out_7 = MBR_OUT ? ALWAYS_OUT : 8'bz;  // Controlled_Buffer controlled_buffer_1

  // Notes on the sheet:
  //   DATA_OUT
endmodule

module MBR_IN (
  input  [7:0] DATA_IN,
  input  MBR_IN,
  input  MBR_OUT,
  input  CLOCK,
  input  MBR_RESET,
  output [7:0] ALWAYS_OUT,
  output [7:0] out_7
);

  Register register_1 (.D(DATA_IN), .en(MBR_IN), .Q(ALWAYS_OUT), .clk(CLOCK), .clr(MBR_RESET));
  assign out_7 = MBR_OUT ? ALWAYS_OUT : 8'bz;  // Controlled_Buffer controlled_buffer_1

  // Notes on the sheet:
  //   DATA_OUT
endmodule
